# Fritzing sketch button_led_resistor (saved by Fritzing 0.8.7b)
breadboards: 1

parts:
  LED1 = LED - 5mm [color="Red (633nm)" package="5 mm [THT]"]
  VCC1 = Battery block 9V
  R1 = Resistor [tolerance=±5% resistance=470 package=THT]
  S1 = Pushbutton [package="[THT]"]

nets:
  N1: LED1.cathode, S1.Pin_3, S1.Pin_4
  N2: LED1.anode, R1.Pin_1
  N3: VCC1.-, S1.Pin_1, S1.Pin_2
  N4: VCC1.+, R1.Pin_0
