# Fritzing sketch progress_bar (saved by Fritzing 0.8.7b)
breadboards: 1

parts:
  Part1 = Arduino Uno (Rev3)
  R2 = Resistor [tolerance=±5% resistance=220 package=THT]
  R3 = Resistor [tolerance=±5% resistance=220 package=THT]
  R4 = Resistor [tolerance=±5% resistance=220 package=THT]
  R5 = Resistor [tolerance=±5% resistance=220 package=THT]
  R6 = Resistor [tolerance=±5% resistance=220 package=THT]
  R1 = Resistor [tolerance=±5% resistance=220 package=THT]
  LED6 = LED - 5mm [color="Green (570nm)" package="5 mm [THT]"]
  LED5 = LED - 5mm [color="Green (570nm)" package="5 mm [THT]"]
  LED4 = LED - 5mm [color="Yellow (595nm)" package="5 mm [THT]"]
  LED3 = LED - 5mm [color="Yellow (595nm)" package="5 mm [THT]"]
  LED1 = LED - 5mm [color="Red (633nm)" package="5 mm [THT]"]
  S1 = Pushbutton [package="[THT]"]
  S2 = Pushbutton [package="[THT]"]
  LED2 = LED - 5mm [color="Red (633nm)" package="5 mm [THT]"]

nets:
  N1: Part1.A0, R1.Pin_1
  N2: Part1.A1, R2.Pin_1
  N3: Part1.A2, R3.Pin_1
  N4: Part1.A3, R4.Pin_1
  N5: Part1.A4/SDA, R5.Pin_1
  N6: Part1.A5/SCL, R6.Pin_1
  N7: Part1.D2, S2.Pin_3, S2.Pin_4
  N8: Part1.D3_PWM, S1.Pin_3, S1.Pin_4
  N9: Part1.GND, LED6.cathode, LED5.cathode, LED4.cathode, LED3.cathode, LED1.cathode, S1.Pin_1, S1.Pin_2, S2.Pin_1, S2.Pin_2, LED2.cathode
  N10: R2.Pin_0, LED2.anode
  N11: R3.Pin_0, LED3.anode
  N12: R4.Pin_0, LED4.anode
  N13: R5.Pin_0, LED5.anode
  N14: R6.Pin_0, LED6.anode
  N15: R1.Pin_0, LED1.anode
