# Fritzing sketch pot_progress_bar (saved by Fritzing 0.8.7b)
breadboards: 1

parts:
  Part1 = Arduino Uno (Rev3)
  R2 = Resistor [tolerance=±5% resistance=220 package=THT]
  R3 = Resistor [tolerance=±5% resistance=220 package=THT]
  R4 = Resistor [tolerance=±5% resistance=220 package=THT]
  R5 = Resistor [tolerance=±5% resistance=220 package=THT]
  R6 = Resistor [tolerance=±5% resistance=220 package=THT]
  R1 = Resistor [tolerance=±5% resistance=220 package=THT]
  LED6 = LED - 5mm [color="Red (633nm)" package="5 mm [THT]"]
  LED5 = LED - 5mm [color="Red (633nm)" package="5 mm [THT]"]
  LED4 = LED - 5mm [color="Yellow (595nm)" package="5 mm [THT]"]
  LED3 = LED - 5mm [color="Yellow (595nm)" package="5 mm [THT]"]
  LED1 = LED - 5mm [color="Green (570nm)" package="5 mm [THT]"]
  LED2 = LED - 5mm [color="Green (570nm)" package="5 mm [THT]"]
  R7 = Rotary Potentiometer (Large) [maximum_resistance=100kΩ package=THT]
  S1 = Pushbutton [package="[THT]"]
  S2 = Pushbutton [package="[THT]"]

nets:
  N1: Part1.A0, R7.wiper
  N2: Part1.A1, S1.Pin_3, S1.Pin_4
  N3: Part1.A2, S2.Pin_1, S2.Pin_2
  N4: Part1.D9_PWM, R4.Pin_1
  N5: Part1.D10_PWM/SS, R5.Pin_1
  N6: Part1.D11_PWM/MOSI, R6.Pin_1
  N7: Part1.GND, LED6.cathode, LED5.cathode, LED4.cathode, LED3.cathode, LED1.cathode, LED2.cathode, R7.leg2, S1.Pin_1, S1.Pin_2, S2.Pin_3, S2.Pin_4
  N8: Part1.D3_PWM, R1.Pin_1
  N9: Part1.D5_PWM, R2.Pin_1
  N10: Part1.D6_PWM, R3.Pin_1
  N11: Part1.5V, R7.leg1
  N12: R2.Pin_0, LED2.anode
  N13: R3.Pin_0, LED3.anode
  N14: R4.Pin_0, LED4.anode
  N15: R5.Pin_0, LED5.anode
  N16: R6.Pin_0, LED6.anode
  N17: R1.Pin_0, LED1.anode
