# Fritzing sketch semaphore (saved by Fritzing 0.8.7b)
breadboards: 1

parts:
  Part1 = Arduino Uno (Rev3)
  R5 = Resistor [tolerance=±5% resistance=220 package=THT]
  R2 = Resistor [tolerance=±5% resistance=220 package=THT]
  LED3 = LED - 5mm [color="Red (633nm)" package="5 mm [THT]"]
  LED4 = LED - 5mm [color="Yellow (595nm)" package="5 mm [THT]"]
  LED5 = LED - 5mm [color="Green (570nm)" package="5 mm [THT]"]
  LED1 = LED - 5mm [color="Green (570nm)" package="5 mm [THT]"]
  LED2 = LED - 5mm [color="Red (633nm)" package="5 mm [THT]"]
  S2 = Pushbutton [package="[THT]"]
  R4 = Resistor [tolerance=±5% resistance=220 package=THT]
  R3 = Resistor [tolerance=±5% resistance=220 package=THT]
  R1 = Resistor [tolerance=±5% resistance=220 package=THT]

nets:
  N1: Part1.D2, S2.Pin_3, S2.Pin_4
  N2: Part1.D3_PWM, R1.Pin_1
  N3: Part1.D4, R2.Pin_1
  N4: Part1.D5_PWM, R3.Pin_1
  N5: Part1.D6_PWM, R4.Pin_1
  N6: Part1.D7, R5.Pin_1
  N7: Part1.GND, LED3.cathode, LED4.cathode, LED5.cathode, LED1.cathode, LED2.cathode, S2.Pin_1, S2.Pin_2
  N8: R5.Pin_0, LED5.anode
  N9: R2.Pin_0, LED2.anode
  N10: LED3.anode, R3.Pin_0
  N11: LED4.anode, R4.Pin_0
  N12: LED1.anode, R1.Pin_0
